// Digital circuit C2-Decimal.dig as structural Verilog
module C2_Decimal (
  input  R2,
  input  R1,
  input  R0,
  input  E,
  output _0,
  output _1,
  output _2,
  output _3,
  output _4,
  output _3_2,
  output _2_2,
  output _1_2
);

  wire not_1_out, not_2_out, not_3_out, not_4_out, not_5_out, not_6_out, not_7_out, not_8_out, not_9_out,
       not_10_out, not_11_out, not_12_out;

  not not_1 (not_1_out, R2);
  not not_2 (not_2_out, R1);
  not not_3 (not_3_out, R0);
  not not_4 (not_4_out, R2);
  not not_5 (not_5_out, R1);
  not not_6 (not_6_out, R2);
  not not_7 (not_7_out, R0);
  not not_8 (not_8_out, R2);
  not not_9 (not_9_out, R1);
  not not_10 (not_10_out, R0);
  not not_11 (not_11_out, R1);
  not not_12 (not_12_out, R0);
  and and_1 (_0, not_1_out, not_2_out, not_3_out, E);
  and and_2 (_1, not_4_out, not_5_out, R0, E);
  and and_3 (_2, not_6_out, R1, not_7_out, E);
  and and_4 (_3, not_8_out, R1, R0, E);
  and and_5 (_4, R2, not_9_out, not_10_out, E);
  and and_6 (_3_2, R2, not_11_out, R0, E);
  and and_7 (_2_2, R2, R1, not_12_out, E);
  and and_8 (_1_2, R2, R1, R0, E);
endmodule
