// Digital circuit C2-Display.dig as structural Verilog
module C2_Display (
  input  R2,
  input  R1,
  input  R0,
  input  E,
  output E1,
  output E2,
  output E3,
  output E4,
  output E5,
  output E6,
  output E7
);

  wire c2_decimal_1__0, c2_decimal_1__1, c2_decimal_1__1_2, c2_decimal_1__2, c2_decimal_1__2_2,
       c2_decimal_1__3, c2_decimal_1__3_2, c2_decimal_1__4, or_1_out, or_2_out, or_3_out;

  C2_Decimal c2_decimal_1 (
    .R2(R2), .R1(R1), .R0(R0), .E(E), ._0(c2_decimal_1__0), ._1(c2_decimal_1__1), ._2(c2_decimal_1__2),
    ._3(c2_decimal_1__3), ._4(c2_decimal_1__4), ._3_2(c2_decimal_1__3_2), ._2_2(c2_decimal_1__2_2),
    ._1_2(c2_decimal_1__1_2));
  or or_1 (or_1_out, c2_decimal_1__1, c2_decimal_1__1_2);
  or or_2 (or_2_out, c2_decimal_1__2, c2_decimal_1__2_2);
  or or_3 (or_3_out, c2_decimal_1__3, c2_decimal_1__3_2);
  or or_4 (E1, c2_decimal_1__0, or_2_out, or_3_out);
  or or_5 (E2, c2_decimal_1__0, or_1_out, or_3_out, c2_decimal_1__4);
  or or_6 (E3, c2_decimal_1__0, or_1_out, c2_decimal_1__4, or_2_out, or_3_out);
  or or_7 (E4, c2_decimal_1__0, or_2_out, or_3_out);
  or or_8 (E5, c2_decimal_1__0, or_2_out);
  or or_9 (E6, c2_decimal_1__0, c2_decimal_1__4);
  or or_10 (E7, or_2_out, or_3_out, c2_decimal_1__4);
endmodule
