// Digital circuit CARRY OUT.dig as structural Verilog
module CARRY_OUT (
  input  plus_C2_C,
  input  plus_C2_E,
  input  plus_SiM_C,
  input  plus_SiM_E,
  input  C2_C,
  input  C2_E,
  input  SiM_C,
  input  SiM_E,
  output C
);

  wire and_1_out, and_2_out, and_3_out, and_4_out;

  and and_1 (and_1_out, plus_C2_C, plus_C2_E);
  and and_2 (and_2_out, plus_SiM_C, plus_SiM_E);
  and and_3 (and_3_out, C2_C, C2_E);
  and and_4 (and_4_out, SiM_C, SiM_E);
  or or_1 (C, and_1_out, and_2_out, and_3_out, and_4_out);
endmodule
