// Digital circuit ConversorSiM-C2.dig as structural Verilog
module ConversorSiM_C2 (
  input  E2,
  input  E1,
  input  E0,
  output S2,
  output S1,
  output S0
);

  wire and_1_out, and_2_out, and_3_out, and_4_out, and_5_out, not_1_out, not_2_out, not_3_out;

  not not_1 (not_1_out, E2);
  not not_2 (not_2_out, E1);
  not not_3 (not_3_out, E0);
  and and_1 (and_1_out, E2, E1);
  and and_2 (and_2_out, E0, E2);
  and and_3 (and_3_out, E0, not_2_out, E2);
  and and_4 (and_4_out, not_3_out, E2, E1);
  and and_5 (and_5_out, E1, not_1_out);
  or or_1 (S2, and_1_out, and_2_out);
  or or_2 (S1, and_3_out, and_4_out, and_5_out);

  assign S0 = E0;
endmodule
