// Digital circuit OVERFLOW.dig as structural Verilog
module OVERFLOW (
  input  plus_C2_O,
  input  plus_C2_E,
  input  plus_SiM_O,
  input  plus_SiM_E,
  input  C2_O,
  input  C2_E,
  input  SiM_O,
  input  SiM_E,
  output O
);

  wire and_1_out, and_2_out, and_3_out, and_4_out;

  and and_1 (and_1_out, plus_C2_O, plus_C2_E);
  and and_2 (and_2_out, plus_SiM_O, plus_SiM_E);
  and and_3 (and_3_out, C2_O, C2_E);
  and and_4 (and_4_out, SiM_O, SiM_E);
  or or_1 (O, and_1_out, and_2_out, and_3_out, and_4_out);
endmodule
