// Digital circuit OpCodi.dig as structural Verilog
module OpCodi (
  input  Op,
  input  Codi,
  output plus_C2,
  output plus_SiM,
  output C2,
  output SiM
);

  wire not_1_out, not_2_out, not_3_out, not_4_out;

  not not_1 (not_1_out, Op);
  not not_2 (not_2_out, Codi);
  not not_3 (not_3_out, Op);
  not not_4 (not_4_out, Codi);
  and and_1 (plus_C2, not_1_out, not_2_out);
  and and_2 (plus_SiM, not_3_out, Codi);
  and and_3 (C2, Op, not_4_out);
  and and_4 (SiM, Op, Codi);
endmodule
