// Digital circuit PUERTASDISPLAY.dig as structural Verilog
module PUERTASDISPLAY (
  input  plus_C2_E1,
  input  plus_C2_E2,
  input  plus_C2_E3,
  input  plus_C2_E4,
  input  plus_C2_E5,
  input  plus_C2_E6,
  input  plus_C2_E7,
  input  plus_SiM_E1,
  input  plus_SiM_E2,
  input  plus_SiM_E3,
  input  plus_SiM_E4,
  input  plus_SiM_E5,
  input  plus_SiM_E6,
  input  plus_SiM_E7,
  input  C2_E1,
  input  C2_E2,
  input  C2_E3,
  input  C2_E4,
  input  C2_E5,
  input  C2_E6,
  input  C2_E7,
  input  SiM_E1,
  input  SiM_E2,
  input  SiM_E3,
  input  SiM_E4,
  input  SiM_E5,
  input  SiM_E6,
  input  SiM_E7,
  output _1,
  output _2,
  output _3,
  output _4,
  output _5,
  output _6,
  output _7
);

  or or_1 (_1, plus_C2_E1, C2_E1, plus_SiM_E1, SiM_E1);
  or or_2 (_2, plus_C2_E2, C2_E2, plus_SiM_E2, SiM_E2);
  or or_3 (_3, plus_C2_E3, C2_E3, plus_SiM_E3, SiM_E3);
  or or_4 (_4, plus_C2_E4, C2_E4, plus_SiM_E4, SiM_E4);
  or or_5 (_5, plus_C2_E5, C2_E5, plus_SiM_E5, SiM_E5);
  or or_6 (_6, plus_C2_E6, C2_E6, plus_SiM_E6, SiM_E6);
  or or_7 (_7, plus_C2_E7, C2_E7, plus_SiM_E7, SiM_E7);
endmodule
