// Digital circuit Restador C2.dig as structural Verilog
module Restador_C2 (
  input  A2,
  input  B2,
  input  A1,
  input  B1,
  input  A0,
  input  B0,
  output C,
  output R2,
  output R1,
  output R0,
  output O
);

  wire full_adder_1_p1, full_adder_2_p1, not_1_out, not_2_out, not_3_out;

  xor xor_1 (O, C, full_adder_1_p1);
  not not_1 (not_1_out, B2);
  // Full_Adder full_adder_1: pin names not known; wires that end beside it: full_adder_1_p1, not_1_out, R2, A2, C
  not not_2 (not_2_out, B1);
  // Full_Adder full_adder_2: pin names not known; wires that end beside it: full_adder_2_p1, not_2_out, R1, A1, full_adder_1_p1
  not not_3 (not_3_out, B0);
  // Full_Adder full_adder_3: pin names not known; wires that end beside it: 1'b1, not_3_out, R0, A0, full_adder_2_p1
endmodule
