// Digital circuit Restador SiM.dig as structural Verilog
module Restador_SiM (
  input  A2,
  input  B2,
  input  A1,
  input  B1,
  input  A0,
  input  B0,
  output C,
  output R2,
  output R1,
  output R0,
  output O
);

  wire and_2_out, and_3_out, conversorsim_c2_1_s0, conversorsim_c2_1_s1, conversorsim_c2_1_s2,
       conversorsim_c2_2_s0, conversorsim_c2_2_s1, conversorsim_c2_2_s2, not_1_out, or_1_out,
       restador_c2_1_c, restador_c2_1_o, restador_c2_1_r2;

  ConversorSiM_C2 conversorsim_c2_1 (
    .E2(A2), .E1(A1), .E0(A0), .S2(conversorsim_c2_1_s2), .S1(conversorsim_c2_1_s1), .S0(conversorsim_c2_1_s0));
  ConversorSiM_C2 conversorsim_c2_2 (
    .E2(B2), .E1(B1), .E0(B0), .S2(conversorsim_c2_2_s2), .S1(conversorsim_c2_2_s1), .S0(conversorsim_c2_2_s0));
  Restador_C2 restador_c2_1 (
    .A2(conversorsim_c2_1_s2), .B2(conversorsim_c2_2_s2), .A1(conversorsim_c2_1_s1),
    .B1(conversorsim_c2_2_s1), .A0(conversorsim_c2_1_s0), .B0(conversorsim_c2_2_s0), .C(restador_c2_1_c),
    .R2(restador_c2_1_r2), .R1(R1), .R0(R0), .O(restador_c2_1_o));
  or or_1 (or_1_out, R1, R0);
  and and_1 (R2, restador_c2_1_r2, or_1_out);
  and and_2 (and_2_out, restador_c2_1_c, O);
  not not_1 (not_1_out, R2);
  and and_3 (and_3_out, not_1_out, restador_c2_1_r2);
  or or_2 (O, and_3_out, restador_c2_1_o);
  or or_3 (C, and_2_out, restador_c2_1_o);
endmodule
