// Digital circuit SiM DISPLAY.dig as structural Verilog
module SiM_DISPLAY (
  input  R2,
  input  R1,
  input  R0,
  input  E,
  output Signo,
  output _0,
  output _1,
  output _2,
  output _3
);

  wire not_1_out, not_2_out, not_3_out, not_4_out;

  not not_1 (not_1_out, R1);
  not not_2 (not_2_out, R0);
  and and_1 (_0, not_1_out, not_2_out, E);
  and and_2 (_1, not_3_out, R0, E);
  not not_3 (not_3_out, R1);
  and and_3 (_2, R1, not_4_out, E);
  not not_4 (not_4_out, R0);
  and and_4 (_3, R1, R0, E);

  assign Signo = R2;
endmodule
