// Digital circuit SiM-DISPLAY.dig as structural Verilog
module SiM_DISPLAY (
  input  R2,
  input  R1,
  input  R0,
  input  E,
  output E1,
  output E2,
  output E3,
  output E4,
  output E5,
  output E6,
  output E7,
  output Signo
);

  wire sim_display_1__1, sim_display_1__2, sim_display_1__3;

  SiM_DISPLAY sim_display_1 (
    .R2(R2), .R1(R1), .R0(R0), .E(E), .Signo(Signo), ._0(E6), ._1(sim_display_1__1), ._2(sim_display_1__2),
    ._3(sim_display_1__3));
  or or_1 (E1, E6, sim_display_1__2, sim_display_1__3);
  or or_2 (E2, E6, sim_display_1__1, sim_display_1__3);
  or or_3 (E3, E6, sim_display_1__1, sim_display_1__2, sim_display_1__3);
  or or_4 (E4, E6, sim_display_1__2, sim_display_1__3);
  or or_5 (E5, E6, sim_display_1__2);
  or or_6 (E7, sim_display_1__2, sim_display_1__3);
endmodule
