// Digital circuit SumadorC2.dig as structural Verilog
module SumadorC2 (
  input  A2,
  input  B2,
  input  A1,
  input  B1,
  input  A0,
  input  B0,
  output C,
  output R2,
  output R1,
  output R0,
  output O
);

  wire full_adder_1_p1, full_adder_2_p1;

  xor xor_1 (O, C, full_adder_1_p1);
  // Full_Adder full_adder_1: pin names not known; wires that end beside it: full_adder_1_p1, B2, R2, A2, C
  // Full_Adder full_adder_2: pin names not known; wires that end beside it: full_adder_2_p1, B1, R1, A1, full_adder_1_p1
  // Half_Adder half_adder_1: pin names not known; wires that end beside it: B0, full_adder_2_p1, A0, R0
endmodule
