// Digital circuit arxiu.dig as structural Verilog
module arxiu (
  input  Op,
  input  Codi,
  input  A2,
  input  B2,
  input  A1,
  input  B1,
  input  A0,
  input  B0,
  output C,
  output O,
  output R2,
  output R1,
  output R0
);

  wire C2, C2_C, c2_display_1_e1, c2_display_1_e2, c2_display_1_e3, c2_display_1_e4, c2_display_1_e5,
       c2_display_1_e6, c2_display_1_e7, c2_display_2_e1, c2_display_2_e2, c2_display_2_e3, c2_display_2_e4,
       c2_display_2_e5, c2_display_2_e6, c2_display_2_e7, c2_display_3_e1, c2_display_3_e2, c2_display_3_e3,
       c2_display_3_e4, c2_display_3_e5, c2_display_3_e6, c2_display_3_e7, c2_display_4_e1, c2_display_4_e2,
       c2_display_4_e3, c2_display_4_e4, c2_display_4_e5, c2_display_4_e6, c2_display_4_e7, C2_O,
       num_display_1__1, num_display_1__2, num_display_1__3, num_display_1__4, num_display_1__5,
       num_display_1__6, num_display_1__7, num_display_2__1, num_display_2__2, num_display_2__3,
       num_display_2__4, num_display_2__5, num_display_2__6, num_display_2__7, or_1_out, or_2_out, or_3_out,
       or_4_out, or_8_out, plus_C2, plus_C2_C, plus_C2_O, plus_SiM, plus_SiM_C, plus_SiM_O,
       puertasdisplay_1__1, puertasdisplay_1__2, puertasdisplay_1__3, puertasdisplay_1__4,
       puertasdisplay_1__5, puertasdisplay_1__6, puertasdisplay_1__7, R0c2, R0c2_plus, R0SiM, R0SiM_plus,
       R1c2, R1c2_plus, R1SiM, R1SiM_plus, R2c2, R2c2_plus, R2SiM, R2SiM_plus, resultados_3_s_a0,
       resultados_3_s_a1, resultados_3_s_a2, resultados_4_s_a0, resultados_4_s_a1, resultados_4_s_a2, S_R0c2,
       S_R0c2_plus, S_R0SiM, S_R0SiM_plus, S_R1c2, S_R1c2_plus, S_R1SiM, S_R1SiM_plus, S_R2c2, S_R2c2_plus,
       S_R2SiM, S_R2SiM_plus, SignoC2, SignoC2_plus, SignoSiM, SignoSiM_plus, SiM, SiM_C, sim_display_1_e1,
       sim_display_1_e2, sim_display_1_e3, sim_display_1_e4, sim_display_1_e5, sim_display_1_e6,
       sim_display_1_e7, sim_display_1_signo, sim_display_2_e1, sim_display_2_e2, sim_display_2_e3,
       sim_display_2_e4, sim_display_2_e5, sim_display_2_e6, sim_display_2_e7, sim_display_2_signo,
       sim_display_3_e1, sim_display_3_e2, sim_display_3_e3, sim_display_3_e4, sim_display_3_e5,
       sim_display_3_e6, sim_display_3_e7, sim_display_3_signo, sim_display_4_e1, sim_display_4_e2,
       sim_display_4_e3, sim_display_4_e4, sim_display_4_e5, sim_display_4_e6, sim_display_4_e7,
       sim_display_4_signo, SiM_O;

  OpCodi opcodi_1 (.Op(Op), .Codi(Codi), .plus_C2(plus_C2), .plus_SiM(plus_SiM), .C2(C2), .SiM(SiM));
  or or_1 (or_1_out, plus_SiM, SiM);
  or or_2 (or_2_out, plus_C2, C2);
  SiM_DISPLAY sim_display_1 (
    .R2(B2), .R1(B1), .R0(B0), .E(or_1_out), .E1(sim_display_1_e1), .E2(sim_display_1_e2),
    .E3(sim_display_1_e3), .E4(sim_display_1_e4), .E5(sim_display_1_e5), .E6(sim_display_1_e6),
    .E7(sim_display_1_e7), .Signo(sim_display_1_signo));
  C2_Display c2_display_1 (
    .R2(B2), .R1(B1), .R0(B0), .E(or_2_out), .E1(c2_display_1_e1), .E2(c2_display_1_e2),
    .E3(c2_display_1_e3), .E4(c2_display_1_e4), .E5(c2_display_1_e5), .E6(c2_display_1_e6),
    .E7(c2_display_1_e7));
  SiM_DISPLAY sim_display_2 (
    .R2(A2), .R1(A1), .R0(A0), .E(or_1_out), .E1(sim_display_2_e1), .E2(sim_display_2_e2),
    .E3(sim_display_2_e3), .E4(sim_display_2_e4), .E5(sim_display_2_e5), .E6(sim_display_2_e6),
    .E7(sim_display_2_e7), .Signo(sim_display_2_signo));
  C2_Display c2_display_2 (
    .R2(A2), .R1(A1), .R0(A0), .E(or_2_out), .E1(c2_display_2_e1), .E2(c2_display_2_e2),
    .E3(c2_display_2_e3), .E4(c2_display_2_e4), .E5(c2_display_2_e5), .E6(c2_display_2_e6),
    .E7(c2_display_2_e7));
  or or_3 (or_3_out, sim_display_1_signo, B2);
  or or_4 (or_4_out, sim_display_2_signo, A2);
  NuM_DISPLAY num_display_1 (
    .C2_E1(sim_display_1_e1), .C2_E2(sim_display_1_e2), .C2_E3(sim_display_1_e3), .C2_E4(sim_display_1_e4),
    .C2_E5(sim_display_1_e5), .C2_E6(sim_display_1_e6), .C2_E7(sim_display_1_e7), .SiM_E1(c2_display_1_e1),
    .SiM_E2(c2_display_1_e2), .SiM_E3(c2_display_1_e3), .SiM_E4(c2_display_1_e4), .SiM_E5(c2_display_1_e5),
    .SiM_E6(c2_display_1_e6), .SiM_E7(c2_display_1_e7), ._1(num_display_1__1), ._2(num_display_1__2),
    ._3(num_display_1__3), ._4(num_display_1__4), ._5(num_display_1__5), ._6(num_display_1__6),
    ._7(num_display_1__7));
  NuM_DISPLAY num_display_2 (
    .C2_E1(sim_display_2_e1), .C2_E2(sim_display_2_e2), .C2_E3(sim_display_2_e3), .C2_E4(sim_display_2_e4),
    .C2_E5(sim_display_2_e5), .C2_E6(sim_display_2_e6), .C2_E7(sim_display_2_e7), .SiM_E1(c2_display_2_e1),
    .SiM_E2(c2_display_2_e2), .SiM_E3(c2_display_2_e3), .SiM_E4(c2_display_2_e4), .SiM_E5(c2_display_2_e5),
    .SiM_E6(c2_display_2_e6), .SiM_E7(c2_display_2_e7), ._1(num_display_2__1), ._2(num_display_2__2),
    ._3(num_display_2__3), ._4(num_display_2__4), ._5(num_display_2__5), ._6(num_display_2__6),
    ._7(num_display_2__7));
  Seven_Seg seven_seg_1 (.a(1'b0), .b(1'b0), .c(1'b0), .d(1'b0), .e(1'b0), .f(1'b0), .g(or_3_out), .dp(1'b0));
  Seven_Seg seven_seg_2 (.a(1'b0), .b(1'b0), .c(1'b0), .d(1'b0), .e(1'b0), .f(1'b0), .g(or_4_out), .dp(1'b0));
  Seven_Seg seven_seg_3 (
    .a(num_display_1__4), .b(num_display_1__3), .c(num_display_1__2), .d(num_display_1__1),
    .e(num_display_1__5), .f(num_display_1__6), .g(num_display_1__7), .dp(1'b0));
  Seven_Seg seven_seg_4 (
    .a(num_display_2__4), .b(num_display_2__3), .c(num_display_2__2), .d(num_display_2__1),
    .e(num_display_2__5), .f(num_display_2__6), .g(num_display_2__7), .dp(1'b0));
  SumadorC2 sumadorc2_1 (
    .A2(A2), .B2(B2), .A1(A1), .B1(B1), .A0(A0), .B0(B0), .C(plus_C2_C), .R2(R2c2_plus), .R1(R1c2_plus),
    .R0(R0c2_plus), .O(plus_C2_O));
  Sumador_SiM sumador_sim_1 (
    .A2(A2), .B2(B2), .A1(A1), .B1(B1), .A0(A0), .B0(B0), .C(plus_SiM_C), .R2(R2SiM_plus), .R1(R1SiM_plus),
    .R0(R0SiM_plus), .O(plus_SiM_O));
  Restador_C2 restador_c2_1 (
    .A2(A2), .B2(B2), .A1(A1), .B1(B1), .A0(A0), .B0(B0), .C(C2_C), .R2(R2c2), .R1(R1c2), .R0(R0c2), .O(C2_O));
  Restador_SiM restador_sim_1 (
    .A2(A2), .B2(B2), .A1(A1), .B1(B1), .A0(A0), .B0(B0), .C(SiM_C), .R2(R2SiM), .R1(R1SiM), .R0(R0SiM),
    .O(SiM_O));
  resultados resultados_1 (
    .E_A2(R2c2_plus), .E_A1(R1c2_plus), .E_A0(R0c2_plus), .E(plus_C2), .S_A2(S_R2c2_plus),
    .S_A1(S_R1c2_plus), .S_A0(S_R0c2_plus));
  resultados resultados_2 (.E_A2(R2c2), .E_A1(R1c2), .E_A0(R0c2), .E(C2), .S_A2(S_R2c2), .S_A1(S_R1c2), .S_A0(S_R0c2));
  resultados resultados_3 (
    .E_A2(R2SiM_plus), .E_A1(R1SiM_plus), .E_A0(R0SiM_plus), .E(plus_SiM), .S_A2(resultados_3_s_a2),
    .S_A1(resultados_3_s_a1), .S_A0(resultados_3_s_a0));
  resultados resultados_4 (
    .E_A2(R2SiM), .E_A1(R1SiM), .E_A0(R0SiM), .E(SiM), .S_A2(resultados_4_s_a2), .S_A1(resultados_4_s_a1),
    .S_A0(resultados_4_s_a0));
  and and_1 (SignoC2_plus, R2c2_plus, plus_C2);
  ConversorSiM_C2 conversorsim_c2_1 (
    .E2(resultados_3_s_a2), .E1(resultados_3_s_a1), .E0(resultados_3_s_a0), .S2(S_R2SiM_plus),
    .S1(S_R1SiM_plus), .S0(S_R0SiM_plus));
  ConversorSiM_C2 conversorsim_c2_2 (
    .E2(resultados_4_s_a2), .E1(resultados_4_s_a1), .E0(resultados_4_s_a0), .S2(S_R2SiM), .S1(S_R1SiM),
    .S0(S_R0SiM));
  C2_Display c2_display_3 (
    .R2(R2c2_plus), .R1(R1c2_plus), .R0(R0c2_plus), .E(plus_C2), .E1(c2_display_3_e1), .E2(c2_display_3_e2),
    .E3(c2_display_3_e3), .E4(c2_display_3_e4), .E5(c2_display_3_e5), .E6(c2_display_3_e6),
    .E7(c2_display_3_e7));
  SiM_DISPLAY sim_display_3 (
    .R2(R2SiM_plus), .R1(R1SiM_plus), .R0(R0SiM_plus), .E(plus_SiM), .E1(sim_display_3_e1),
    .E2(sim_display_3_e2), .E3(sim_display_3_e3), .E4(sim_display_3_e4), .E5(sim_display_3_e5),
    .E6(sim_display_3_e6), .E7(sim_display_3_e7), .Signo(sim_display_3_signo));
  C2_Display c2_display_4 (
    .R2(R2c2), .R1(R1c2), .R0(R0c2), .E(C2), .E1(c2_display_4_e1), .E2(c2_display_4_e2),
    .E3(c2_display_4_e3), .E4(c2_display_4_e4), .E5(c2_display_4_e5), .E6(c2_display_4_e6),
    .E7(c2_display_4_e7));
  and and_2 (SignoC2, R2c2, C2);
  SiM_DISPLAY sim_display_4 (
    .R2(R2SiM), .R1(R1SiM), .R0(R0SiM), .E(SiM), .E1(sim_display_4_e1), .E2(sim_display_4_e2),
    .E3(sim_display_4_e3), .E4(sim_display_4_e4), .E5(sim_display_4_e5), .E6(sim_display_4_e6),
    .E7(sim_display_4_e7), .Signo(sim_display_4_signo));
  and and_3 (SignoSiM_plus, sim_display_3_signo, plus_SiM);
  and and_4 (SignoSiM, sim_display_4_signo, SiM);
  or or_5 (R2, S_R2c2_plus, S_R2c2, S_R2SiM_plus, S_R2SiM);
  or or_6 (R1, S_R1c2_plus, S_R1c2, S_R1SiM_plus, S_R1SiM);
  or or_7 (R0, S_R0c2_plus, S_R0c2, S_R0SiM_plus, S_R0SiM);
  PUERTASDISPLAY puertasdisplay_1 (
    .plus_C2_E1(c2_display_3_e1), .plus_C2_E2(c2_display_3_e2), .plus_C2_E3(c2_display_3_e3),
    .plus_C2_E4(c2_display_3_e4), .plus_C2_E5(c2_display_3_e5), .plus_C2_E6(c2_display_3_e6),
    .plus_C2_E7(c2_display_3_e7), .plus_SiM_E1(sim_display_3_e1), .plus_SiM_E2(sim_display_3_e2),
    .plus_SiM_E3(sim_display_3_e3), .plus_SiM_E4(sim_display_3_e4), .plus_SiM_E5(sim_display_3_e5),
    .plus_SiM_E6(sim_display_3_e6), .plus_SiM_E7(sim_display_3_e7), .C2_E1(c2_display_4_e1),
    .C2_E2(c2_display_4_e2), .C2_E3(c2_display_4_e3), .C2_E4(c2_display_4_e4), .C2_E5(c2_display_4_e5),
    .C2_E6(c2_display_4_e6), .C2_E7(c2_display_4_e7), .SiM_E1(sim_display_4_e1), .SiM_E2(sim_display_4_e2),
    .SiM_E3(sim_display_4_e3), .SiM_E4(sim_display_4_e4), .SiM_E5(sim_display_4_e5),
    .SiM_E6(sim_display_4_e6), .SiM_E7(sim_display_4_e7), ._1(puertasdisplay_1__1), ._2(puertasdisplay_1__2),
    ._3(puertasdisplay_1__3), ._4(puertasdisplay_1__4), ._5(puertasdisplay_1__5), ._6(puertasdisplay_1__6),
    ._7(puertasdisplay_1__7));
  or or_8 (or_8_out, SignoC2_plus, SignoSiM_plus, SignoC2, SignoSiM);
  OVERFLOW overflow_1 (
    .plus_C2_O(plus_C2_O), .plus_C2_E(plus_C2), .plus_SiM_O(plus_SiM_O), .plus_SiM_E(plus_SiM), .C2_O(C2_O),
    .C2_E(C2), .SiM_O(SiM_O), .SiM_E(SiM), .O(O));
  CARRY_OUT carry_out_1 (
    .plus_C2_C(plus_C2_C), .plus_C2_E(plus_C2), .plus_SiM_C(plus_SiM_C), .plus_SiM_E(plus_SiM), .C2_C(C2_C),
    .C2_E(C2), .SiM_C(SiM_C), .SiM_E(SiM), .C(C));
  Seven_Seg seven_seg_5 (.a(1'b0), .b(1'b0), .c(1'b0), .d(1'b0), .e(1'b0), .f(1'b0), .g(or_8_out), .dp(1'b0));
  Seven_Seg seven_seg_6 (
    .a(puertasdisplay_1__4), .b(puertasdisplay_1__3), .c(puertasdisplay_1__2), .d(puertasdisplay_1__1),
    .e(puertasdisplay_1__5), .f(puertasdisplay_1__6), .g(puertasdisplay_1__7), .dp(1'b0));

  // Other names for the same wires on the sheet: C2_E = C2; plus_C2_E = plus_C2; plus_SiM_E = plus_SiM; SiM_E = SiM

  // Notes on the sheet:
  //   ENTRADA B
  //   ENTRADA A
  //   RESULTADO
endmodule
