// Digital circuit resultados.dig as structural Verilog
module resultados (
  input  E_A2,
  input  E_A1,
  input  E_A0,
  input  E,
  output S_A2,
  output S_A1,
  output S_A0
);

  and and_1 (S_A2, E_A2, E);
  and and_2 (S_A1, E_A1, E);
  and and_3 (S_A0, E_A0, E);
endmodule
