// Digital circuit arxiu.dig as structural Verilog
module arxiu (
  input  C,
  input  m1,
  input  m0,
  output z2,
  output z1,
  output z0
);

  wire and_1_out, and_2_out, and_3_out, and_4_out, and_5_out, and_6_out, and_7_out, and_8_out, and_9_out,
       and_10_out, and_11_out, and_12_out, and_13_out, not_1_out, not_2_out, not_3_out, not_4_out, not_5_out,
       or_1_out, or_2_out, or_3_out;

  not not_1 (not_1_out, m1);
  not not_2 (not_2_out, m0);
  not not_3 (not_3_out, z2);
  not not_4 (not_4_out, z1);
  not not_5 (not_5_out, z0);
  and and_1 (and_1_out, not_1_out, m0, not_5_out, not_4_out, not_3_out);
  and and_2 (and_2_out, not_1_out, m0, z0, z2);
  and and_3 (and_3_out, m1, m0, z1);
  and and_4 (and_4_out, not_2_out, z0, z1, not_3_out);
  and and_5 (and_5_out, not_2_out, not_4_out, z2);
  and and_6 (and_6_out, not_5_out, z1, z2);
  and and_7 (and_7_out, not_1_out, m0, not_5_out, not_4_out);
  and and_8 (and_8_out, m1, z0, not_4_out);
  and and_9 (and_9_out, not_2_out, z0, not_4_out);
  and and_10 (and_10_out, not_2_out, not_5_out, z1);
  and and_11 (and_11_out, m0, z0, z1);
  and and_12 (and_12_out, not_1_out, not_5_out);
  and and_13 (and_13_out, not_2_out, not_5_out);
  or or_1 (or_1_out, and_7_out, and_8_out, and_9_out, and_10_out, and_11_out);
  or or_2 (or_2_out, and_12_out, and_13_out);
  or or_3 (or_3_out, and_1_out, and_2_out, and_3_out, and_4_out, and_5_out, and_6_out);
  D_FF Q_2_n (.D(or_3_out), .C(C), .Q(z2));  // open: nQ
  D_FF Q_1_n (.D(or_1_out), .C(C), .Q(z1));  // open: nQ
  D_FF Q_0_n (.D(or_2_out), .C(C), .Q(z0));  // open: nQ

  // Other names for the same wires on the sheet: Q_0_n = z0; Q_1_n = z1; Q_2_n = z2
endmodule

/* Test case BNSSascendente:
C m1 m0 z2 z1 z0
0 0 0 0 0 0
C 0 0 0 0 1
C 0 0 0 1 0
C 0 0 0 1 1
C 0 0 1 0 0
C 0 0 1 0 1
C 0 0 1 1 0
C 0 0 1 1 1
C 0 0 0 0 0
*/

/* Test case BNSSdescendente:
C m1 m0 z2 z1 z0
0 0 1 0 0 0
C 0 1 1 1 1
C 0 1 1 1 0
C 0 1 1 0 1
C 0 1 1 0 0
C 0 1 0 1 1
C 0 1 0 1 0
C 0 1 0 0 1
C 0 1 0 0 0
C 0 1 1 1 1
*/

/* Test case C2ascendente:
C m1 m0 z2 z1 z0
0 1 0 0 0 0
C 1 0 0 0 1
C 1 0 0 1 0
C 1 0 0 1 1
C 1 0 1 0 0
C 1 0 1 0 1
C 1 0 1 1 0
C 1 0 1 1 1
C 1 0 0 0 0
*/

/* Test case desplazamiento:
C m1 m0 z2 z1 z0
#desplazamiento para 001 y 010 y 100 y 000
0 0 0 0 0 0
C 0 0 0 0 1
C 1 1 0 1 0
C 1 1 1 0 0
C 1 1 0 0 0
#desplazamiento para 011 110 y 100 y 000
C 0 0 0 0 1
C 0 0 0 1 0
C 0 0 0 1 1
C 1 1 1 1 0
C 1 1 1 0 0
C 1 1 0 0 0 
#desplazamiento para 101 010 100 y 000
C 0 0 0 0 1
C 0 0 0 1 0
C 0 0 0 1 1
C 0 0 1 0 0
C 0 0 1 0 1
C 1 1 0 1 0
C 1 1 1 0 0
C 1 1 0 0 0
#desplazamiento para 111
C 0 0 0 0 1
C 0 0 0 1 0
C 0 0 0 1 1
C 0 0 1 0 0
C 0 0 1 0 1
C 0 0 1 1 0
C 0 0 1 1 1
C 1 1 1 1 0
C 1 1 1 0 0
C 1 1 0 0 0
*/
